# Fritzing sketch Dual 8 Bit Shift Registers (saved by Fritzing 0.9.3b)
circuit board: 8.46667cm x 5.64444cm
breadboards: 1

parts:
  IC1 = SHIFT REGISTER [package=dil16]
  IC2 = SHIFT REGISTER [package=dil16]
  Arduino_Uno = Arduino Uno (Rev3)

nets (from the breadboard view):
  GND: IC1.GND, IC2.GND, Arduino_Uno.GND
  N1: IC1.QH*, IC2.SER
  VCC: IC1.SCL, IC1.VCC, IC2.SCL, IC2.VCC, Arduino_Uno.5V
  N2: IC1.SCK, IC2.SCK
  N3: IC1.RCK, IC2.RCK, Arduino_Uno.D10_PWM/SS
  N4: IC1.G, IC2.G, Arduino_Uno.D9_PWM
  N5: IC1.SER, Arduino_Uno.D8
  N6: IC1.QA, Arduino_Uno.D7
