# Fritzing sketch Tri 8 Bit Shift Registers (saved by Fritzing 0.9.3b)
circuit board: 8.46667cm x 5.64444cm
breadboards: 1

parts:
  IC1 = SHIFT REGISTER [package=dil16]
  IC2 = SHIFT REGISTER [package=dil16]
  Arduino_Uno = Arduino Uno (Rev3)
  IC3 = SHIFT REGISTER [package=dil16]

nets:
  GND: IC1.GND, IC2.GND, Arduino_Uno.GND, IC3.GND
  N1: IC1.QH*, IC2.SER
  N2: IC1.SCK, IC2.SCK, Arduino_Uno.D6_PWM, IC3.SCK
  N3: IC1.RCK, IC1.SER, IC2.RCK, Arduino_Uno.D9_PWM, Arduino_Uno.D7, IC3.RCK
  VCC: IC1.G, IC1.VCC, IC2.G, IC2.VCC, Arduino_Uno.D8, Arduino_Uno.5V, IC3.G, IC3.VCC
  N4: IC2.QH*, IC3.SER
